// Logisim project G2.circ as structural Verilog: 2 circuits, main circuit main
module main (
  output [3:0] out_1,
  output [1:0] out_2
);

  wire ALUSrc, and_1_out, Branch, Jump, MemRead, MemtoReg, MemWrite, mips_alu_1_p4, RegDst,
       registerfile_1_p6, RegWrite, Tick;
  wire [4:0] multiplexer_1_out;
  wire [5:0] Control_p1;
  wire [23:0] bit_extender_3_out;
  wire [25:0] undriven;
  wire [27:0] bit_extender_1_out, shifter_1_out;
  wire [31:0] adder_1_p3, adder_2_p3, bit_extender_2_out, mips_alu_1_p5, mips_ram_1_p6, multiplexer_2_out,
       multiplexer_3_out, multiplexer_4_out, PC_q, registerfile_1_p1, registerfile_1_p7, shifter_2_out;

  Clock clock_1 (.out(Tick));
  Register #(.width(32)) PC (.D(multiplexer_4_out), .Q(PC_q), .clk(Tick));  // open: en, clr
  // PLA Control: pin names not known; wires that end beside it: Control_p1
  // Adder adder_1: pin names not known; wires that end beside it: PC_q, 32'h4, adder_1_p3
  // MIPSProgramROM mipsprogramrom_1: pin names not known; wires that end beside it: PC_q, Tick, RegDst
  assign bit_extender_1_out = {{2{1'b0}}, undriven};  // Bit_Extender bit_extender_1
  Shifter #(.width(28)) shifter_1 (.in(bit_extender_1_out), .\dist (5'b00010), .out(shifter_1_out));
  Multiplexer #(.width(5), .enable("false")) multiplexer_1 (
    .in0(undriven[20:16]), .in1(undriven[15:11]), .out(multiplexer_1_out), .sel(RegDst));
  // RegisterFile registerfile_1: pin names not known; wires that end beside it: registerfile_1_p1, RegWrite, multiplexer_1_out, undriven[25:21], undriven[20:16], registerfile_1_p6, registerfile_1_p7
  assign bit_extender_2_out = {{16{undriven[15]}}, undriven[15:0]};  // Bit_Extender bit_extender_2
  Multiplexer #(.width(32), .enable("false")) multiplexer_2 (
    .in0(registerfile_1_p7), .in1(bit_extender_2_out), .out(multiplexer_2_out), .sel(ALUSrc));
  ALU_control alu_control_1 (.in_1({out_2, undriven[5:0]}), .out_2(out_1));
  Shifter #(.width(32)) shifter_2 (.in(bit_extender_2_out), .\dist (5'b00010), .out(shifter_2_out));
  // MIPS_ALU mips_alu_1: pin names not known; wires that end beside it: registerfile_1_p6, multiplexer_2_out, out_1, mips_alu_1_p4, mips_alu_1_p5
  // Adder adder_2: pin names not known; wires that end beside it: adder_1_p3, shifter_2_out, adder_2_p3
  Bit_Extender #(.in_width(32), .out_width(24)) bit_extender_3 (.in(mips_alu_1_p5), .out(bit_extender_3_out));
  Multiplexer #(.width(32), .enable("false")) multiplexer_3 (
    .in0(adder_1_p3), .in1(adder_2_p3), .out(multiplexer_3_out), .sel(and_1_out));
  and and_1 (and_1_out, Branch, mips_alu_1_p4);
  Multiplexer #(.width(32), .enable("false")) multiplexer_4 (
    .in0(multiplexer_3_out), .in1({shifter_1_out, adder_1_p3[31:28]}), .out(multiplexer_4_out), .sel(Jump));
  // MIPS_RAM mips_ram_1: pin names not known; wires that end beside it: bit_extender_3_out, registerfile_1_p7, MemWrite, MemRead, Tick, mips_ram_1_p6
  Multiplexer #(.width(32), .enable("false")) multiplexer_5 (
    .in0(mips_alu_1_p5), .in1(mips_ram_1_p6), .out(registerfile_1_p1), .sel(MemtoReg));

  // Other names for the same wires on the sheet: ALUOp[1:0] = out_2
endmodule

module ALU_control (
  input  [7:0] in_1,
  output [3:0] out_2
);

  // PLA pla_1: pin names not known; wires that end beside it: in_1, out_2
endmodule
