// Logisim project sandbox.circ as structural Verilog: 5 circuits, main circuit main
module main (
  output [31:0] Fetched_Instruction,
  output [31:0] Next_Instruction,
  output [5:0] Operation_Code,
  output [3:0] out_4,
  output [1:0] out_5
);

  wire ALUSrc, and_1_out, Branch, Jump, MemRead, MemToReg, MemWrite, mips_alu_1_p4, not_1_out, RegDst,
       RegWrite, Tick;
  wire [3:0] alu_control_1_out_2, mips_alu_1_p3;
  wire [4:0] multiplexer_3_out, multiplexer_4_out;
  wire [23:0] bit_extender_4_out;
  wire [25:0] Control_p2;
  wire [27:0] bit_extender_1_out, shifter_1_out;
  wire [31:0] adder_1_p3, adder_2_p4, adder_3_p3, bit_extender_2_out, bit_extender_3_out, id_ex_1_a__out,
       id_ex_1_b__out, id_ex_1_inst___out, id_ex_1_pc__out, if_id_1_pc__out, mips_alu_1_p2, mips_alu_1_p5,
       mips_ram_1_p6, multiplexer_1_out, multiplexer_2_out, multiplexer_8_out, multiplexer_9_out,
       multiplexer_10_out, PC_q, registerfile_1_p7, registerfile_1_p8, shifter_2_out, shifter_3_out;
  wire [31:28] undriven;

  Multiplexer #(.width(32), .enable("false")) multiplexer_1 (
    .in0(multiplexer_9_out), .in1(adder_1_p3), .out(multiplexer_1_out), .sel(not_1_out));
  not not_1 (not_1_out, Jump);
  Register #(.width(32)) PC (.D(multiplexer_1_out), .Q(PC_q), .clk(Tick));  // open: en, clr
  // Adder adder_1: pin names not known; wires that end beside it: PC_q, 32'h4, adder_1_p3
  // Adder adder_2: pin names not known; wires that end beside it: PC_q, 32'h8, PC_q, adder_2_p4
  Clock clock_1 (.out(Tick));
  // MIPSProgramROM mipsprogramrom_1: pin names not known; wires that end beside it: Next_Instruction
  IF_ID if_id_1 (
    .Clock(Tick), .PC__in(adder_1_p3), .Inst___in(Next_Instruction), .PC__out(if_id_1_pc__out),
    .Inst___out(Fetched_Instruction));
  // PLA Control: pin names not known; wires that end beside it: Fetched_Instruction[31:26], Control_p2
  assign bit_extender_1_out = {{2{1'b0}}, Control_p2};  // Bit_Extender bit_extender_1
  assign bit_extender_2_out = {{6{1'b0}}, Fetched_Instruction[25:0]};  // Bit_Extender bit_extender_2
  Multiplexer #(.width(32), .enable("false")) multiplexer_2 (
    .in0(multiplexer_10_out), .in1(adder_2_p4), .out(multiplexer_2_out), .sel(Jump));
  Shifter #(.width(28)) shifter_1 (.in(bit_extender_1_out), .\dist (5'b00010), .out(shifter_1_out));
  Shifter #(.width(32)) shifter_2 (.in(bit_extender_2_out), .\dist (5'b00010), .out(shifter_2_out));
  Multiplexer #(.width(5), .enable("false")) multiplexer_3 (
    .in0(multiplexer_4_out), .in1({5{1'b1}}), .out(multiplexer_3_out), .sel(Jump));
  Multiplexer #(.width(5), .enable("false")) multiplexer_4 (
    .in0(Fetched_Instruction[20:16]), .in1(Fetched_Instruction[15:11]), .out(multiplexer_4_out), .sel(RegDst));
  // RegisterFile registerfile_1: pin names not known; wires that end beside it: multiplexer_2_out, Tick, RegWrite, multiplexer_3_out, Fetched_Instruction[25:21], Fetched_Instruction[20:16], registerfile_1_p7, registerfile_1_p8
  assign bit_extender_3_out = {{16{Fetched_Instruction[15]}}, Fetched_Instruction[15:0]};  // Bit_Extender bit_extender_3
  ID_EX id_ex_1 (
    .Clock(Tick), .PC__in(if_id_1_pc__out), .A__in(registerfile_1_p7), .B__in(registerfile_1_p8),
    .Inst___in(bit_extender_3_out), .PC__out(id_ex_1_pc__out), .A__out(id_ex_1_a__out),
    .B__out(id_ex_1_b__out), .inst___out(id_ex_1_inst___out));
  Multiplexer #(.width(32), .enable("false")) multiplexer_5 (
    .in0({shifter_1_out, undriven}), .sel(RegWrite));  // open: in1, out
  Shifter #(.width(32)) shifter_3 (.in(id_ex_1_inst___out), .\dist (5'b00010), .out(shifter_3_out));
  // MIPS_ALU mips_alu_1: pin names not known; wires that end beside it: id_ex_1_a__out, mips_alu_1_p2, mips_alu_1_p3, mips_alu_1_p4, mips_alu_1_p5
  Multiplexer #(.width(32), .enable("false")) multiplexer_6 (
    .in0(id_ex_1_b__out), .in1(id_ex_1_inst___out), .out(mips_alu_1_p2), .sel(ALUSrc));
  Multiplexer #(.width(4), .enable("false")) multiplexer_7 (
    .in0(alu_control_1_out_2), .in1(out_4), .out(mips_alu_1_p3), .sel(alu_control_1_out_2[3]));
  ALU_control alu_control_1 (.in_1({out_5, Fetched_Instruction[5:0]}), .out_2(alu_control_1_out_2));
  // Adder adder_3: pin names not known; wires that end beside it: id_ex_1_pc__out, shifter_3_out, adder_3_p3
  Imm__Ctrl imm_ctrl_1 (.in_1(Fetched_Instruction[28:26]), .out_2(out_4));
  and and_1 (and_1_out, Branch, mips_alu_1_p4);
  Bit_Extender #(.in_width(32), .out_width(24)) bit_extender_4 (.in(mips_alu_1_p5), .out(bit_extender_4_out));
  Multiplexer #(.width(32), .enable("false")) multiplexer_8 (
    .in0(id_ex_1_pc__out), .in1(adder_3_p3), .out(multiplexer_8_out), .sel(and_1_out));
  Multiplexer #(.width(32), .enable("false")) multiplexer_9 (
    .in0(multiplexer_8_out), .in1(shifter_2_out), .out(multiplexer_9_out), .sel(Jump));
  // MIPS_RAM mips_ram_1: pin names not known; wires that end beside it: bit_extender_4_out, id_ex_1_b__out, MemWrite, MemRead, Tick, mips_ram_1_p6
  Multiplexer #(.width(32), .enable("false")) multiplexer_10 (
    .in0(mips_alu_1_p5), .in1(mips_ram_1_p6), .out(multiplexer_10_out), .sel(MemToReg));

  assign Operation_Code = Fetched_Instruction[31:26];

  // Other names for the same wires on the sheet: ALUOp[1:0] = out_5
endmodule

module ALU_control (
  input  [7:0] in_1,
  output [3:0] out_2
);

  // PLA pla_1: pin names not known; wires that end beside it: in_1, out_2
endmodule

module Imm__Ctrl (
  input  [2:0] in_1,
  output [3:0] out_2
);

  // PLA Imm__Ctrl: pin names not known; wires that end beside it: in_1, out_2
endmodule

module IF_ID (
  input  Clock,
  input  [31:0] PC__in,
  input  [31:0] Inst___in,
  output [31:0] PC__out,
  output [31:0] Inst___out
);

  Register #(.width(32)) register_1 (.D(PC__in), .Q(PC__out), .clk(Clock));  // open: en, clr
  Register #(.width(32)) register_2 (.D(Inst___in), .Q(Inst___out), .clk(Clock));  // open: en, clr

  // Other names for the same wires on the sheet: Tick = Clock
endmodule

module ID_EX (
  input  Clock,
  input  [31:0] PC__in,
  input  [31:0] A__in,
  input  [31:0] B__in,
  input  [31:0] Inst___in,
  output [31:0] PC__out,
  output [31:0] A__out,
  output [31:0] B__out,
  output [31:0] inst___out
);

  Register #(.width(32)) register_1 (.D(PC__in), .Q(PC__out), .clk(Clock));  // open: en, clr
  Register #(.width(32)) register_2 (.D(A__in), .Q(A__out), .clk(Clock));  // open: en, clr
  Register #(.width(32)) register_3 (.D(B__in), .Q(B__out), .clk(Clock));  // open: en, clr
  Register #(.width(32)) register_4 (.D(Inst___in), .Q(inst___out), .clk(Clock));  // open: en, clr

  // Other names for the same wires on the sheet: Tick = Clock
endmodule
